# Fritzing sketch circuit_diagram (saved by Fritzing 1.0.5)

parts:
  XIAO_ESP32S3_Plus1 = Seeed Studio XIAO ESP32S3 Plus [chip_label="XIAO ESP32S3 Plus" package="DIP (Dual Inline)"]
  FSR_sensor = Basic Force Sensing Resistor (FSR) [package=THT]
  R2 = Resistor [tolerance=±5% resistance=220 package="0805 [SMD]"]
  ENS160+AHT21 = ENS160 AHT21
  U1 = LIPO-110mAh [package=lipo-110]
  S1 = Toggle Switch [package=THT]
  GY-MAX4466 = Adafruit MAX4466 Electret Microphone Amplifier [part_number="Adafruit #1063"]

nets:
  N1: XIAO_ESP32S3_Plus1.D1, XIAO_ESP32S3_Plus1.5V, R2.Pin_0, U1.+
  N2: XIAO_ESP32S3_Plus1.D2, GY-MAX4466.OUT
  N3: XIAO_ESP32S3_Plus1.D4, ENS160+AHT21.Pin_5
  N4: XIAO_ESP32S3_Plus1.D5, ENS160+AHT21.Pin_4
  3V3: XIAO_ESP32S3_Plus1.3V3, ENS160+AHT21.Pin_1, GY-MAX4466.VCC
  GND: XIAO_ESP32S3_Plus1.GND, FSR_sensor.pin_2, ENS160+AHT21.Pin_3, ENS160+AHT21.Pin_6, S1.L2, GY-MAX4466.GND
  N5: FSR_sensor.pin_1, R2.Pin_1
  N6: U1.-, S1.COM

custom parts:
  Seeed Studio XIAO ESP32S3 Plus: Seeed Studio XIAO ESP32S3 Plus, powered by ESP32-S3's 240MHz Xtensa 32-bit LX7 dual-core processor, brings more SMD pins to the tiny versatile XIAO ESP32S3. While maintaining all the powerful features including WiFi and BLE 5.0 wireless connectivities, 2.4GHz Rod antenna, and ultra-low power consumption of 14μA in deep sleep mode with lithium battery charging management, the Plus variant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
  ENS160 AHT21: The CO2 Gas- Air- Sensor is based on ENS160 in combination with an AHT21 Temperature Humidity Sensor.
  Adafruit MAX4466 Electret Microphone Amplifier: Add an ear to your project with this well-designed electret microphone amplifier. This fully assembled and tested board comes with a 20-20KHz electret microphone soldered on. For the amplification, we use the Maxim MAX4466, an op-amp specifically designed for this delicate task! The amplifier has excellent power supply noise rejection, so this amplifier sounds really good and isn't nearly as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
