# Fritzing sketch circuit_diagram2 (saved by Fritzing 1.0.5)

parts:
  XIAO_ESP32S3_Plus2 = Seeed Studio XIAO ESP32S3 Plus [chip_label="XIAO ESP32S3 Plus" package="DIP (Dual Inline)"]
  U2 = LIPO-110mAh [package=lipo-110]
  S2 = Toggle Switch [package=THT]
  MPU6050 = InvenSense MPU6050
  MAX30102 = MakerFocus MAX30102

nets:
  N1: XIAO_ESP32S3_Plus2.D3, MPU6050.INT
  N2: XIAO_ESP32S3_Plus2.D4, MPU6050.SDA, MAX30102.SDA
  N3: XIAO_ESP32S3_Plus2.D5, MPU6050.SCL, MAX30102.SCL
  GND: XIAO_ESP32S3_Plus2.GND, S2.L2, MPU6050.GND, MPU6050.AD0, MAX30102.GND
  5V: XIAO_ESP32S3_Plus2.5V, U2.+, MPU6050.VCC, MAX30102.VIN
  N4: U2.-, S2.COM

custom parts:
  Seeed Studio XIAO ESP32S3 Plus: Seeed Studio XIAO ESP32S3 Plus, powered by ESP32-S3's 240MHz Xtensa 32-bit LX7 dual-core processor, brings more SMD pins to the tiny versatile XIAO ESP32S3. While maintaining all the powerful features including WiFi and BLE 5.0 wireless connectivities, 2.4GHz Rod antenna, and ultra-low power consumption of 14μA in deep sleep mode with lithium battery charging management, the Plus variant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
  MakerFocus MAX30102: Oximeter module using the MAX30102 chip. As usual, if you want the mounting holes in pcb, you need to drag a hole over the pad in silkscreen to actually drill the hole (by default they are not drilled)
